// Logisim project Bicicleta.circ as structural Verilog: 2 circuits, main circuit main
module main (
  input  A,
  input  B,
  input  C,
  output L1,
  output L2,
  output L3,
  output L4,
  output L5
);

  wire and_1_out, or_1_out;

  and and_1 (and_1_out, B, C);
  or or_1 (or_1_out, B, C);
  or or_2 (L1, A, B, C);
  or or_3 (L2, A, B);
  or or_4 (L3, A, and_1_out);
  and and_2 (L5, A, or_1_out);
  DotMatrix #(.matrixcols(1), .matrixrows(5)) dotmatrix_1 (.col0({L5, A, L3, L2, L1}));

  assign L4 = A;
endmodule

module Com_Clock (
);

  wire and_1_out, B_out, C_out, or_1_out;
  wire [4:0] or_2_out;

  Clock #(.highDuration(4), .lowDuration(4)) A (.out(or_2_out[3]));
  Clock C (.out(C_out));
  Clock #(.highDuration(2), .lowDuration(2)) B (.out(B_out));
  and and_1 (and_1_out, B_out, C_out);
  or or_1 (or_1_out, B_out, C_out);
  or or_2 (or_2_out[0], or_2_out[3], B_out, C_out);
  or or_3 (or_2_out[1], or_2_out[3], B_out);
  or or_4 (or_2_out[2], or_2_out[3], and_1_out);
  and and_2 (or_2_out[4], or_2_out[3], or_1_out);
  DotMatrix #(.matrixcols(1), .matrixrows(5)) dotmatrix_1 (.col0(or_2_out));

  // Notes on the sheet:
  //   L1
  //   L2
  //   L3
  //   L4
  //   L5
endmodule
