// Logisim project Codificador.circ as structural Verilog
module \Codificador___entrada_em_nível_alto  (
  input  A0,
  input  A1,
  input  A2,
  input  A3,
  input  A4,
  input  A5,
  input  A6,
  input  A7,
  output O0,
  output O1,
  output O2
);

  or or_1 (O0, A1, A3, A5, A7);
  or or_2 (O1, A3, A3, A6, A7);
  or or_3 (O2, A4, A5, A6, A7);

  // Notes on the sheet:
  //   Codificador com Entradas Ativas em Nível Alto
endmodule

module \Codificador___entrada_em_nível_baixo  (
  input  A0,
  input  A1,
  input  A2,
  input  A3,
  input  A4,
  input  A5,
  input  A6,
  input  A7,
  output O0,
  output O1,
  output O2
);

  wire not_1_out, not_2_out, not_3_out, not_4_out, not_5_out, not_6_out, not_7_out, not_8_out, not_9_out,
       not_10_out, not_11_out, not_12_out;

  not not_1 (not_1_out, A1);
  not not_2 (not_2_out, A3);
  not not_3 (not_3_out, A5);
  not not_4 (not_4_out, A7);
  not not_5 (not_5_out, A2);
  not not_6 (not_6_out, A3);
  not not_7 (not_7_out, A6);
  not not_8 (not_8_out, A7);
  not not_9 (not_9_out, A4);
  not not_10 (not_10_out, A5);
  not not_11 (not_11_out, A6);
  not not_12 (not_12_out, A7);
  or or_1 (O0, not_1_out, not_2_out, not_3_out, not_4_out);
  or or_2 (O1, not_5_out, not_6_out, not_7_out, not_8_out);
  or or_3 (O2, not_9_out, not_10_out, not_11_out, not_12_out);

  // Notes on the sheet:
  //   Codificador com Entradas Ativas em Nível Baixo
endmodule
