// Logisim project DE MORGAN.circ as structural Verilog: 1 circuit, main circuit main
module main (
  input  A,
  input  B,
  input  A_2,
  input  B_2,
  output out_5,
  output out_6
);

  wire and_1_out, nand_1_out, nor_1_out, not_1_out, not_2_out, not_3_out, not_4_out, or_1_out;

  not not_1 (not_1_out, A_2);
  not not_2 (not_2_out, B_2);
  nor nor_1 (nor_1_out, A_2, B_2);
  and and_1 (and_1_out, not_1_out, not_2_out);
  xnor xnor_1 (out_6, nor_1_out, and_1_out);
  not not_3 (not_3_out, A);
  not not_4 (not_4_out, B);
  nand nand_1 (nand_1_out, A, B);
  or or_1 (or_1_out, not_3_out, not_4_out);
  xnor xnor_2 (out_5, nand_1_out, or_1_out);

  // Notes on the sheet:
  //   (A + B)' = A' . B'
  //   LEIS DE DE MORGAN
  //   (A . B)' = A' + B'
endmodule
