// Logisim project Decodificador.circ as structural Verilog
module Decodificador_BCD (
  input  Enable,
  input  A,
  input  B,
  input  C,
  input  D,
  output D9,
  output D8,
  output D7,
  output D6,
  output D5,
  output D4,
  output D3,
  output D2,
  output D1,
  output D0
);

  wire and_10_out, and_11_out, not_1_out, not_2_out, not_3_out, not_4_out, not_5_out, not_6_out, not_7_out,
       not_8_out, not_9_out, not_10_out, not_11_out, not_12_out, not_13_out, not_14_out, not_15_out;

  not not_1 (not_1_out, D);
  not not_2 (not_2_out, D);
  not not_3 (not_3_out, C);
  not not_4 (not_4_out, C);
  not not_5 (not_5_out, D);
  not not_6 (not_6_out, B);
  not not_7 (not_7_out, B);
  not not_8 (not_8_out, D);
  not not_9 (not_9_out, A);
  not not_10 (not_10_out, B);
  not not_11 (not_11_out, C);
  not not_12 (not_12_out, A);
  not not_13 (not_13_out, B);
  not not_14 (not_14_out, C);
  not not_15 (not_15_out, D);
  and and_1 (D9, Enable, A, D);
  and and_2 (D8, Enable, A, not_1_out);
  and and_3 (D7, Enable, B, C, D);
  and and_4 (D6, Enable, B, C, not_2_out);
  and and_5 (D5, Enable, B, not_3_out, D);
  and and_6 (D4, Enable, B, not_4_out, not_5_out);
  and and_7 (D3, Enable, not_6_out, C, D);
  and and_8 (D2, Enable, not_7_out, C, not_8_out);
  and and_9 (D1, Enable, not_9_out, not_10_out, not_11_out, D);
  and and_10 (and_10_out, Enable, not_12_out, not_13_out, not_14_out, not_15_out);
  and and_11 (and_11_out, Enable, A, C);
  or or_1 (D0, and_10_out, and_11_out);
endmodule

module Decodificador_BCD_7_Segmentos (
  input  A,
  input  B,
  input  C,
  input  D,
  output a_2,
  output b_2,
  output c_2,
  output d_2,
  output e,
  output f,
  output g
);

  wire and_1_out, and_2_out, and_3_out, and_4_out, and_5_out, and_6_out, and_7_out, and_8_out, and_9_out,
       and_10_out, and_11_out, and_12_out, and_13_out, and_14_out, and_15_out, and_16_out, and_17_out,
       and_18_out, and_19_out, and_20_out, and_21_out, and_22_out, and_23_out, not_1_out, not_2_out,
       not_3_out, not_4_out, not_5_out, not_6_out, not_7_out, not_8_out, not_9_out, not_10_out, not_11_out,
       not_12_out, not_13_out, not_14_out, not_15_out, not_16_out, not_17_out, not_18_out, not_19_out,
       not_20_out, not_21_out, not_22_out, not_23_out, not_24_out, not_25_out, not_26_out, not_27_out,
       not_28_out, not_29_out;

  not not_1 (not_1_out, B);
  not not_2 (not_2_out, D);
  not not_3 (not_3_out, A);
  not not_4 (not_4_out, B);
  not not_5 (not_5_out, A);
  not not_6 (not_6_out, C);
  not not_7 (not_7_out, D);
  not not_8 (not_8_out, B);
  not not_9 (not_9_out, C);
  not not_10 (not_10_out, A);
  not not_11 (not_11_out, B);
  not not_12 (not_12_out, C);
  not not_13 (not_13_out, A);
  not not_14 (not_14_out, A);
  not not_15 (not_15_out, B);
  not not_16 (not_16_out, D);
  not not_17 (not_17_out, B);
  not not_18 (not_18_out, D);
  not not_19 (not_19_out, C);
  not not_20 (not_20_out, B);
  not not_21 (not_21_out, D);
  not not_22 (not_22_out, D);
  not not_23 (not_23_out, C);
  not not_24 (not_24_out, D);
  not not_25 (not_25_out, C);
  not not_26 (not_26_out, D);
  not not_27 (not_27_out, B);
  not not_28 (not_28_out, C);
  not not_29 (not_29_out, D);
  and and_1 (and_1_out, not_1_out, not_2_out);
  and and_2 (and_2_out, B, D);
  and and_3 (and_3_out, not_3_out, not_4_out);
  and and_4 (and_4_out, not_5_out, not_6_out, not_7_out);
  and and_5 (and_5_out, not_8_out, not_9_out);
  and and_6 (and_6_out, not_10_out, C, D);
  and and_7 (and_7_out, not_11_out, not_12_out);
  and and_8 (and_8_out, not_13_out, D);
  and and_9 (and_9_out, not_14_out, B);
  and and_10 (and_10_out, not_15_out, not_16_out);
  and and_11 (and_11_out, not_17_out, C);
  and and_12 (and_12_out, C, not_18_out);
  and and_13 (and_13_out, B, not_19_out, D);
  and and_14 (and_14_out, not_20_out, not_21_out);
  and and_15 (and_15_out, C, not_22_out);
  and and_16 (and_16_out, A, C);
  and and_17 (and_17_out, A, B);
  and and_18 (and_18_out, not_23_out, not_24_out);
  and and_19 (and_19_out, B, not_25_out);
  and and_20 (and_20_out, B, not_26_out);
  and and_21 (and_21_out, not_27_out, C);
  and and_22 (and_22_out, B, not_28_out);
  and and_23 (and_23_out, B, not_29_out);
  or or_1 (a_2, and_1_out, C, and_2_out, A);
  or or_2 (b_2, and_3_out, and_4_out, and_5_out, and_6_out);
  or or_3 (c_2, and_7_out, and_8_out, and_9_out);
  or or_4 (d_2, and_10_out, and_11_out, and_12_out, and_13_out, A);
  or or_5 (e, and_14_out, and_15_out, and_16_out, and_17_out);
  or or_6 (f, and_18_out, and_19_out, and_20_out, A);
  or or_7 (g, and_21_out, and_22_out, and_23_out, A);
  _7_Segment_Display u_7_segment_display_1 (.g(g), .f(f), .a(a_2), .b(b_2), .e(e), .d(d_2), .c(c_2));  // open: dp
endmodule

module Decodificador_BCD_7_Segmentos_Clock (
  output a,
  output b,
  output c,
  output d,
  output e,
  output f,
  output g
);

  wire A_out, and_1_out, and_2_out, and_3_out, and_4_out, and_5_out, and_6_out, and_7_out, and_8_out,
       and_9_out, and_10_out, and_11_out, and_12_out, and_13_out, and_14_out, and_15_out, and_16_out,
       and_17_out, and_18_out, and_19_out, and_20_out, and_21_out, and_22_out, and_23_out, B_out, C_out,
       D_out, not_1_out, not_2_out, not_3_out, not_4_out, not_5_out, not_6_out, not_7_out, not_8_out,
       not_9_out, not_10_out, not_11_out, not_12_out, not_13_out, not_14_out, not_15_out, not_16_out,
       not_17_out, not_18_out, not_19_out, not_20_out, not_21_out, not_22_out, not_23_out, not_24_out,
       not_25_out, not_26_out, not_27_out, not_28_out, not_29_out;

  Clock #(.highDuration(8), .lowDuration(8)) u_A (.out(A_out));
  Clock #(.highDuration(4), .lowDuration(4)) u_B (.out(B_out));
  Clock #(.highDuration(2), .lowDuration(2)) u_C (.out(C_out));
  Clock u_D (.out(D_out));
  not not_1 (not_1_out, B_out);
  not not_2 (not_2_out, D_out);
  not not_3 (not_3_out, A_out);
  not not_4 (not_4_out, B_out);
  not not_5 (not_5_out, A_out);
  not not_6 (not_6_out, C_out);
  not not_7 (not_7_out, D_out);
  not not_8 (not_8_out, B_out);
  not not_9 (not_9_out, C_out);
  not not_10 (not_10_out, A_out);
  not not_11 (not_11_out, B_out);
  not not_12 (not_12_out, C_out);
  not not_13 (not_13_out, A_out);
  not not_14 (not_14_out, A_out);
  not not_15 (not_15_out, B_out);
  not not_16 (not_16_out, D_out);
  not not_17 (not_17_out, B_out);
  not not_18 (not_18_out, D_out);
  not not_19 (not_19_out, C_out);
  not not_20 (not_20_out, B_out);
  not not_21 (not_21_out, D_out);
  not not_22 (not_22_out, D_out);
  not not_23 (not_23_out, C_out);
  not not_24 (not_24_out, D_out);
  not not_25 (not_25_out, C_out);
  not not_26 (not_26_out, D_out);
  not not_27 (not_27_out, B_out);
  not not_28 (not_28_out, C_out);
  not not_29 (not_29_out, D_out);
  and and_1 (and_1_out, not_1_out, not_2_out);
  and and_2 (and_2_out, B_out, D_out);
  and and_3 (and_3_out, not_3_out, not_4_out);
  and and_4 (and_4_out, not_5_out, not_6_out, not_7_out);
  and and_5 (and_5_out, not_8_out, not_9_out);
  and and_6 (and_6_out, not_10_out, C_out, D_out);
  and and_7 (and_7_out, not_11_out, not_12_out);
  and and_8 (and_8_out, not_13_out, D_out);
  and and_9 (and_9_out, not_14_out, B_out);
  and and_10 (and_10_out, not_15_out, not_16_out);
  and and_11 (and_11_out, not_17_out, C_out);
  and and_12 (and_12_out, C_out, not_18_out);
  and and_13 (and_13_out, B_out, not_19_out, D_out);
  and and_14 (and_14_out, not_20_out, not_21_out);
  and and_15 (and_15_out, C_out, not_22_out);
  and and_16 (and_16_out, A_out, C_out);
  and and_17 (and_17_out, A_out, B_out);
  and and_18 (and_18_out, not_23_out, not_24_out);
  and and_19 (and_19_out, B_out, not_25_out);
  and and_20 (and_20_out, B_out, not_26_out);
  and and_21 (and_21_out, not_27_out, C_out);
  and and_22 (and_22_out, B_out, not_28_out);
  and and_23 (and_23_out, B_out, not_29_out);
  or or_1 (a, and_1_out, C_out, and_2_out, A_out);
  or or_2 (b, and_3_out, and_4_out, and_5_out, and_6_out);
  or or_3 (c, and_7_out, and_8_out, and_9_out);
  or or_4 (d, and_10_out, and_11_out, and_12_out, and_13_out, A_out);
  or or_5 (e, and_14_out, and_15_out, and_16_out, and_17_out);
  or or_6 (f, and_18_out, and_19_out, and_20_out, A_out);
  or or_7 (g, and_21_out, and_22_out, and_23_out, A_out);
  _7_Segment_Display u_7_segment_display_1 (.g(g), .f(f), .a(a), .b(b), .e(e), .d(d), .c(c));  // open: dp
endmodule
