// Logisim project Indicador de Nível de Bateria.circ as structural Verilog: 1 circuit, main circuit main
module main (
);

  wire and_1_out, and_2_out, and_3_out, not_1_out, or_1_out;
  wire [3:0] slider_1_out;

  Slider #(.width(4), .value('hc)) slider_1 (.out(slider_1_out));
  and and_1 (and_1_out, slider_1_out[3], slider_1_out[0]);
  and and_2 (and_2_out, slider_1_out[3], slider_1_out[1]);
  and and_3 (and_3_out, slider_1_out[3], slider_1_out[2]);
  or or_1 (or_1_out, and_1_out, and_2_out, and_3_out);
  LED led_1 (.in(or_1_out));
  not not_1 (not_1_out, or_1_out);
  LED led_2 (.in(not_1_out));

  // Notes on the sheet:
  //   Saída A/D (Bateria)
  //   A
  //   B
  //   C
  //   D
  //   S
  //   VD
  //   VM
endmodule
