// Logisim project Osciloscopio.circ as structural Verilog: 2 circuits, main circuit Osciloscópio
module \Osciloscópio  (
  input  A,
  input  B,
  input  C,
  input  Clock,
  input  Enable
);

  wire and_1_out, and_2_out, and_3_out, and_4_out, Clear_out, not_1_out, not_2_out, or_1_out, or_2_out;

  not not_1 (not_1_out, A);
  not not_2 (not_2_out, B);
  and and_1 (and_1_out, not_1_out, C);
  and and_2 (and_2_out, B, C);
  and and_3 (and_3_out, A, not_2_out);
  and and_4 (and_4_out, A, C);
  or or_1 (or_1_out, and_1_out, and_2_out);
  or or_2 (or_2_out, and_3_out, and_4_out);
  Button Clear (.out(Clear_out));
  // Digital_Oscilloscope Osciloscópio: pin names not known; wires that end beside it: Clock, or_1_out, or_2_out, Enable, Clear_out
endmodule

module Clock (
  input  in_1
);

  wire displaydecoder_1_p2, displaydecoder_1_p3, displaydecoder_1_p4, displaydecoder_1_p5,
       displaydecoder_1_p6, displaydecoder_1_p7, displaydecoder_1_p8;
  wire [2:0] clock_1_out;

  Clock_part clock_1 (.out(clock_1_out[0]));
  Clock_part #(.highDuration(2), .lowDuration(2)) clock_2 (.out(clock_1_out[1]));
  Clock_part #(.highDuration(4), .lowDuration(4)) clock_3 (.out(clock_1_out[2]));
  // Digital_Oscilloscope digital_oscilloscope_1: pin names not known; wires that end beside it: clock_1_out[0], clock_1_out[1], clock_1_out[2], in_1
  // DisplayDecoder displaydecoder_1: pin names not known; wires that end beside it: {1'b0, clock_1_out}, displaydecoder_1_p2, displaydecoder_1_p3, displaydecoder_1_p4, displaydecoder_1_p5, displaydecoder_1_p6, displaydecoder_1_p7, displaydecoder_1_p8
  _7_Segment_Display u_7_segment_display_1 (
    .g(displaydecoder_1_p8), .f(displaydecoder_1_p7), .a(displaydecoder_1_p2), .b(displaydecoder_1_p3),
    .e(displaydecoder_1_p6), .d(displaydecoder_1_p5), .c(displaydecoder_1_p4));  // open: dp
endmodule
