// Logisim project PORTAS UNIVERSAIS.circ as structural Verilog
module NOR (
  input  A,
  input  A_2,
  input  B,
  input  A_3,
  input  B_2,
  output A_prime,
  output A_B,
  output A_B_2
);

  wire nor_2_out, nor_3_out, nor_5_out;

  nor nor_1 (A_prime, A_2, A_2);
  nor nor_2 (nor_2_out, A_3, A_3);
  nor nor_3 (nor_3_out, B_2, B_2);
  nor nor_4 (A_B_2, nor_2_out, nor_3_out);
  nor nor_5 (nor_5_out, A, B);
  nor nor_6 (A_B, nor_5_out, nor_5_out);

  // Notes on the sheet:
  //   NOT (Inversora)
  //   PORTA UNIVERSAL NOR
  //   AND (E)
  //   OR (OU)
endmodule

module NAND (
  input  A,
  input  A_2,
  input  B,
  input  A_3,
  input  B_2,
  output A_prime,
  output A_B,
  output A_B_2
);

  wire nand_2_out, nand_3_out, nand_4_out;

  nand nand_1 (A_prime, A_2, A_2);
  nand nand_2 (nand_2_out, A_3, A_3);
  nand nand_3 (nand_3_out, B_2, B_2);
  nand nand_4 (nand_4_out, A, B);
  nand nand_5 (A_B_2, nand_2_out, nand_3_out);
  nand nand_6 (A_B, nand_4_out, nand_4_out);

  // Notes on the sheet:
  //   NOT (Inversora)
  //   PORTA UNIVERSAL NAND
  //   OR (OU)
  //   AND (E)
endmodule
