// Logisim project PortasUniversais.circ as structural Verilog: 1 circuit, main circuit Portas Universais
module Portas_Universais (
  input  A,
  input  A_2,
  input  B,
  input  B_2,
  input  A_3,
  input  in_6,
  input  A_4,
  input  A_5,
  input  B_3,
  input  B_4,
  input  A_6,
  input  A_7,
  input  B_5,
  input  B_6,
  output out_15,
  output out_16,
  output out_17,
  output out_18,
  output out_19,
  output out_20,
  output out_21,
  output out_22
);

  wire nand_2_out, nand_3_out, nand_4_out, nor_1_out, nor_2_out, nor_3_out;

  nand nand_1 (out_17, A_3, A_3);
  nand nand_2 (nand_2_out, A_4, A_4);
  nand nand_3 (nand_3_out, B_4, B_4);
  nand nand_4 (nand_4_out, A_7, B_5);
  nand nand_5 (out_15, A, B);
  nand nand_6 (out_20, nand_2_out, nand_3_out);
  nand nand_7 (out_21, nand_4_out, nand_4_out);
  nor nor_1 (nor_1_out, A_5, B_3);
  nor nor_2 (nor_2_out, A_6, A_6);
  nor nor_3 (nor_3_out, B_6, B_6);
  nor nor_4 (out_16, A_2, B_2);
  nor nor_5 (out_18, in_6, in_6);
  nor nor_6 (out_19, nor_1_out, nor_1_out);
  nor nor_7 (out_22, nor_2_out, nor_3_out);

  // Notes on the sheet:
  //   Porta Inversora
  //   Porta OU
  //   Porta E
  //   PORTAS NAND (NÃO E)
  //   PORTAS UNIVERSAIS
  //   PORTAS NOR (NÃO OU)
endmodule
