// Logisim project Somadores.circ as structural Verilog: 2 circuits, main circuit Meio Somador
module Meio_Somador (
  input  A,
  input  B,
  output Soma,
  output Vai_Um
);

  xor xor_1 (Soma, A, B);
  and and_1 (Vai_Um, A, B);

  // Notes on the sheet:
  //   Meio Somador
  //   Autor: Mauro Hemerly Gazzani
endmodule

module Somador_Completo (
  input  A,
  input  B,
  input  Vem_Um,
  input  Vem_Um_2,
  input  A_2,
  input  B_2,
  output Soma,
  output Vai_Um,
  output Soma_2,
  output Vai_Um_2
);

  wire and_1_out, and_2_out, meio_somador_1_soma, meio_somador_1_vai_um, meio_somador_2_vai_um, xor_1_out;

  and and_1 (and_1_out, A, B);
  Meio_Somador meio_somador_1 (.A(A_2), .B(B_2), .Soma(meio_somador_1_soma), .Vai_Um(meio_somador_1_vai_um));
  xor xor_1 (xor_1_out, A, B);
  and and_2 (and_2_out, xor_1_out, Vem_Um);
  xor xor_2 (Soma, xor_1_out, Vem_Um);
  or or_1 (Vai_Um, and_1_out, and_2_out);
  Meio_Somador meio_somador_2 (.A(Vem_Um_2), .B(meio_somador_1_soma), .Soma(Soma_2), .Vai_Um(meio_somador_2_vai_um));
  or or_2 (Vai_Um_2, meio_somador_2_vai_um, meio_somador_1_vai_um);

  // Notes on the sheet:
  //   Somador Completo
  //   Somador Completo a partir de 2 Meio Somadores
endmodule
