// Logisim project XOR-NXOR.circ as structural Verilog: 2 circuits, main circuit XOR
module XOR (
  input  A,
  input  B,
  output S
);

  wire and_1_out, and_2_out, not_1_out, not_2_out;

  not not_1 (not_1_out, A);
  not not_2 (not_2_out, B);
  and and_1 (and_1_out, A, not_2_out);
  or or_1 (S, and_1_out, and_2_out);
  and and_2 (and_2_out, not_1_out, B);

  // Notes on the sheet:
  //   Exclusivo
  //   XOR
endmodule

module NXOR (
  input  in_1,
  input  in_2,
  input  A,
  input  B,
  output out_5,
  output S
);

  wire and_1_out, and_2_out, not_1_out, not_3_out, or_1_out, xor_1_s;

  XOR xor_1 (.A(in_1), .B(in_2), .S(xor_1_s));
  not not_1 (not_1_out, A);
  not not_2 (out_5, xor_1_s);
  not not_3 (not_3_out, B);
  and and_1 (and_1_out, A, not_3_out);
  and and_2 (and_2_out, not_1_out, B);
  or or_1 (or_1_out, and_1_out, and_2_out);
  not not_4 (S, or_1_out);

  // Notes on the sheet:
  //   NXOR
  //   "Coincidência"
endmodule
